// Digital circuit microcode.dig as structural Verilog
module microcode (
  input  [7:0] d0,
  input  c,
  output uPC_CLR,
  output PC_INC,
  output PCL_RD,
  output PCH_RD,
  output IR0_RD,
  output IR1_RD,
  output IR2_RD,
  output PC_WR_AB,
  output SP_WR_AB,
  output SP_INC,
  output SP_DEC,
  output RS_WR_AB,
  output [2:0] REG_RD,
  output [2:0] DB_WR_DEV
);

  wire [3:0] uPC_out;
  wire [7:2] rom_1_d;

  ROM #(.AddrBits(12), .Bits(8)) rom_1 (.A({uPC_out, d0}), .sel(1'b1), .D({rom_1_d, DB_WR_DEV[2:1]}));
  Counter #(.Bits(4)) uPC (.en(1'b1), .C(c), .clr(uPC_CLR), .out(uPC_out));  // open: ovf
  ROM #(.AddrBits(12), .Bits(8)) rom_2 (
    .A({uPC_out, d0}), .sel(1'b1), .D({DB_WR_DEV[0], REG_RD, RS_WR_AB, SP_DEC, SP_INC, SP_WR_AB}));
  ROM #(.AddrBits(12), .Bits(8)) rom_3 (
    .A({uPC_out, d0}), .sel(1'b1), .D({PC_WR_AB, IR2_RD, IR1_RD, IR0_RD, PCH_RD, PCL_RD, PC_INC, uPC_CLR}));
endmodule
